# Fritzing sketch esp32supermini-PIR-LED (saved by Fritzing 0.9.5d)
breadboards: 1

parts:
  A1 = Esp32-c3 super mini
  LED1 = smd LED [color="Red (633nm)" package="0603 [SMD]"]
  R2 = PHOTOCELL [package=photocell-kit]
  J1 = Piezo Speaker
  A2 = PIR sensor (non-bendable legs)
  R3 = Resistor [tolerance=±5% resistance=220 package="2010 [SMD]"]
  R4 = Resistor [tolerance=±5% resistance=220 package="2010 [SMD]"]

nets:
  N1: A1.Pin_6, J1.pin2
  N2: A1.Pin_9, R2.P$2, R4.Pin_0
  N3: A1.Pin_12, A2.SIG
  N4: A1.Pin_13, R3.Pin_1
  N5: A1.Pin_14, R2.P$1, A2.VDD
  N6: A1.Pin_15, LED1.cathode, J1.pin1, A2.GND, R4.Pin_1
  N7: LED1.anode, R3.Pin_0

custom parts:
  Esp32-c3 super mini: ESP32-C3 Development Board ESP32 SuperMini Development Board ESP32 Development Board WiFi Bluetooth.
  PIR sensor (non-bendable legs): Generic PIR sensor
